# Fritzing sketch nodemci+oled+dht22 (saved by Fritzing 0.8.7b)

parts:
  RHT1 = Humidity and Temperature Sensor RHT03
  D1_D0_DC = OLED Monochrome 128x64 1.3 inch [part_number=938]
  U1 = NodeMCU V3.0

nets:
  VCC: RHT1.Vcc, D1_D0_DC.DC_SA0, D1_D0_DC.3.3V, U1.3V3
  N1: RHT1.Data-signal, U1.D7
  GND: RHT1.GND_2, D1_D0_DC.GND, U1.GND
  N2: D1_D0_DC.MOSI_SDA, U1.D3
  N3: D1_D0_DC.SCLK_SCK, U1.D4
  N4: D1_D0_DC.RESET, U1.D2

custom parts:
  OLED Monochrome 128x64 1.3 inch: These displays are small, only about 1.3" diagonal, but very readable due to the high contrast of an OLED display. This display is made of 128x64 individual white OLED pixels, each one is turned on or off by the controller chip. Because the display makes its own light, no backlight is required. This reduces the power required to run the OLED and is why the display has such high contrast; we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
  NodeMCU V3.0: ESP8266 based NodeMCU
